// Logisim project lab1 (1).circ as structural Verilog: 1 circuit, main circuit main
module main (
);

  wire and_1_out, and_2_out, and_3_out, and_4_out, and_5_out, and_6_out, and_7_out, and_8_out, and_9_out,
       and_10_out, and_11_out, clock_1_out, clock_2_out, d_ff_1_qn, d_ff_2_qn, d_ff_3_q, d_ff_3_qn,
       main_1_p6, main_1_p7, main_1_p8, main_1_p9, main_1_p10, main_1_p11, main_1_p12, main_1_p13, not_1_out,
       not_2_out, not_3_out, not_4_out, not_5_out, not_6_out, not_7_out, or_1_out, or_2_out, or_3_out,
       or_4_out, or_5_out;
  wire [6:0] counter_1_q;
  wire [7:0] ram_1_data;

  Counter #(.width(7), .max('h7f)) counter_1 (.Q(counter_1_q), .clk(clock_1_out));  // open: load, D, count, carry, clr
  Clock clock_1 (.out(clock_1_out));
  RAM #(.addrWidth(7)) ram_1 (.addr(counter_1_q), .data(ram_1_data), .clk(clock_2_out));  // open: sel, ld, clr
  Clock clock_2 (.out(clock_2_out));
  // petro__1__main main_1: pin names not known; wires that end beside it: ram_1_data[0], ram_1_data[1], ram_1_data[4], ram_1_data[5], ram_1_data[6], main_1_p6, main_1_p7, main_1_p8, main_1_p9, main_1_p10, main_1_p11, main_1_p12, main_1_p13
  // Probe on clock_2_out
  and and_1 (and_1_out, clock_2_out, main_1_p8);
  not not_1 (not_1_out, clock_2_out);
  not not_2 (not_2_out, clock_2_out);
  or or_1 (or_1_out, main_1_p13, clock_2_out);
  and and_2 (and_2_out, main_1_p9, not_1_out);
  and and_3 (and_3_out, main_1_p10, not_2_out);
  not not_3 (not_3_out, or_1_out);
  and and_4 (and_4_out, ram_1_data[7], and_1_out);
  // Probe on d_ff_1_qn
  D_Flip_Flop d_ff_1 (.clk(and_2_out), .D(d_ff_3_q), .Qn(d_ff_1_qn));  // open: Q, preset, en, reset
  // Probe on d_ff_2_qn
  D_Flip_Flop d_ff_2 (.clk(and_3_out), .D(d_ff_3_q), .Qn(d_ff_2_qn));  // open: Q, preset, en, reset
  and and_5 (and_5_out, d_ff_1_qn, main_1_p6);
  and and_6 (and_6_out, d_ff_2_qn, main_1_p7);
  or or_2 (or_2_out, and_6_out, and_4_out);
  and and_7 (and_7_out, or_2_out, and_5_out);
  or or_3 (or_3_out, and_5_out, or_2_out);
  not not_4 (not_4_out, main_1_p12);
  and and_8 (and_8_out, and_7_out, main_1_p12);
  and and_9 (and_9_out, or_3_out, not_4_out);
  or or_4 (or_4_out, and_8_out, and_9_out);
  not not_5 (not_5_out, or_4_out);
  not not_6 (not_6_out, main_1_p11);
  and and_10 (and_10_out, not_5_out, main_1_p11);
  and and_11 (and_11_out, or_4_out, not_6_out);
  or or_5 (or_5_out, and_10_out, and_11_out);
  D_Flip_Flop d_ff_3 (.clk(not_3_out), .D(or_5_out), .Q(d_ff_3_q), .Qn(d_ff_3_qn));  // open: preset, en, reset
  not not_7 (not_7_out, d_ff_3_qn);
  // Probe on not_7_out
endmodule
